// Logisim project S1-T11.circ as structural Verilog: 14 circuits, main circuit main
module main (
  input  [15:0] in_1,
  input  [3:0] Ticket_Price,
  output [3:0] Balance,
  output [2:0] Queue_Length,
  output [3:0] Balance_2,
  output [2:0] Queue_Length_2,
  output [3:0] Balance_3,
  output [2:0] Queue_Length_3,
  output [3:0] Balance_4,
  output [2:0] Queue_Length_4,
  output bike,
  output car,
  output truck,
  output [3:0] Balance_5,
  output [2:0] Queue_Length_5,
  output [3:0] Balance_6,
  output [2:0] Queue_Length_6
);

  wire and_1_out, and_2_out, and_3_out, decoder_1_out1, decoder_1_out2, decoder_1_out3, decoder_1_out4,
       decoder_1_out5, decoder_1_out6, Dequeue_Vehicle_out, Enqueue_Vehicle_out, luhn_gate_1_valid,
       multiplexer_1_out, multiplexer_2_out, multiplexer_3_out, multiplexer_4_out, multiplexer_5_out,
       multiplexer_6_out, not_1_out, not_2_out, payment_processor_1_clock, payment_processor_1_m,
       payment_processor_1_out_6, payment_processor_1_out_7, payment_processor_2_clock,
       payment_processor_2_m, payment_processor_2_out_6, payment_processor_2_out_7,
       payment_processor_3_clock, payment_processor_3_m, payment_processor_3_out_6,
       payment_processor_3_out_7, payment_processor_4_clock, payment_processor_4_m,
       payment_processor_4_out_6, payment_processor_4_out_7, payment_processor_5_clock,
       payment_processor_5_m, payment_processor_5_out_6, payment_processor_5_out_7,
       payment_processor_6_clock, payment_processor_6_m, payment_processor_6_out_6,
       payment_processor_6_out_7, Priority_Check_common_vehicle, Priority_Check_priority_vehicle,
       Priority_Velhicle_out, Vehicle_Type_out;
  wire [2:0] lane_separation_1_final_lane__binary;

  Button Priority_Velhicle (.out(Priority_Velhicle_out));
  vehicle_priority Priority_Check (
    .in_1(Priority_Velhicle_out), .Priority_Vehicle(Priority_Check_priority_vehicle),
    .Common_Vehicle(Priority_Check_common_vehicle));
  luhn_gate luhn_gate_1 (
    .MSB(in_1[0]), .in_2(in_1[1]), .in_3(in_1[2]), .LSB(in_1[3]), .MSB_2(in_1[4]), .in_6(in_1[5]),
    .in_7(in_1[6]), .LSB_2(in_1[7]), .MSB_3(in_1[8]), .in_10(in_1[9]), .in_11(in_1[10]), .LSB_3(in_1[11]),
    .enable(Priority_Check_common_vehicle), .MSB_4(in_1[12]), .in_15(in_1[13]), .in_16(in_1[14]),
    .LSB_4(in_1[15]), .valid(luhn_gate_1_valid));
  LED led_1 (.in(Priority_Check_priority_vehicle));
  LED led_2 (.in(and_1_out));
  and and_1 (and_1_out, not_2_out, not_1_out);
  not not_1 (not_1_out, and_2_out);
  not not_2 (not_2_out, Priority_Check_priority_vehicle);
  and and_2 (and_2_out, luhn_gate_1_valid, Priority_Check_common_vehicle);
  Button Vehicle_Type (.out(Vehicle_Type_out));
  segregate Segregator (.in_1(and_3_out), .trucks(truck), .cars(car), .bikes(bike));
  and and_3 (and_3_out, and_2_out, Vehicle_Type_out);
  Clock Dequeue_Vehicle (.out(Dequeue_Vehicle_out));
  Button Enqueue_Vehicle (.out(Enqueue_Vehicle_out));
  lane_separation lane_separation_1 (
    .Lane_1(Queue_Length), .Lane_3(Queue_Length_3), .Lane_5(Queue_Length_5), .Lane_2(Queue_Length_2),
    .Lane_4(Queue_Length_4), .Lane_6(Queue_Length_6),
    .Final_Lane__Binary(lane_separation_1_final_lane__binary), .Vehicle_type({bike, car}));
  Decoder #(.select(3), .disabled(0)) decoder_1 (
    .out1(decoder_1_out1), .out2(decoder_1_out2), .out3(decoder_1_out3), .out4(decoder_1_out4),
    .out5(decoder_1_out5), .out6(decoder_1_out6), .sel(lane_separation_1_final_lane__binary),
    .en(Enqueue_Vehicle_out));  // open: out0, out7
  Multiplexer #(.disabled(0)) multiplexer_1 (
    .in0(1'b1), .in1(Enqueue_Vehicle_out), .out(multiplexer_1_out), .sel(decoder_1_out1));  // open: en
  Multiplexer #(.disabled(0)) multiplexer_2 (
    .in0(1'b1), .in1(Enqueue_Vehicle_out), .out(multiplexer_2_out), .sel(decoder_1_out2));  // open: en
  Multiplexer #(.disabled(0)) multiplexer_3 (
    .in0(1'b1), .in1(Enqueue_Vehicle_out), .out(multiplexer_3_out), .sel(decoder_1_out3));  // open: en
  Multiplexer #(.disabled(0)) multiplexer_4 (
    .in0(1'b1), .in1(Enqueue_Vehicle_out), .out(multiplexer_4_out), .sel(decoder_1_out4));  // open: en
  Multiplexer #(.disabled(0)) multiplexer_5 (
    .in0(1'b1), .in1(Enqueue_Vehicle_out), .out(multiplexer_5_out), .sel(decoder_1_out5));  // open: en
  Multiplexer #(.disabled(0)) multiplexer_6 (
    .in0(1'b1), .in1(Enqueue_Vehicle_out), .out(multiplexer_6_out), .sel(decoder_1_out6));  // open: en
  payment_processor payment_processor_1 (
    .Queue_Length(Queue_Length), .decrement(Dequeue_Vehicle_out), .Balance(Balance),
    .Ticket_Price(Ticket_Price), .increment(multiplexer_1_out), .out_6(payment_processor_1_out_6),
    .out_7(payment_processor_1_out_7), .M(payment_processor_1_m), .Clock(payment_processor_1_clock));
  payment_processor payment_processor_2 (
    .Queue_Length(Queue_Length_2), .decrement(Dequeue_Vehicle_out), .Balance(Balance_2),
    .Ticket_Price(Ticket_Price), .increment(multiplexer_2_out), .out_6(payment_processor_2_out_6),
    .out_7(payment_processor_2_out_7), .M(payment_processor_2_m), .Clock(payment_processor_2_clock));
  payment_processor payment_processor_3 (
    .Queue_Length(Queue_Length_3), .decrement(Dequeue_Vehicle_out), .Balance(Balance_3),
    .Ticket_Price(Ticket_Price), .increment(multiplexer_3_out), .out_6(payment_processor_3_out_6),
    .out_7(payment_processor_3_out_7), .M(payment_processor_3_m), .Clock(payment_processor_3_clock));
  payment_processor payment_processor_4 (
    .Queue_Length(Queue_Length_4), .decrement(Dequeue_Vehicle_out), .Balance(Balance_4),
    .Ticket_Price(Ticket_Price), .increment(multiplexer_4_out), .out_6(payment_processor_4_out_6),
    .out_7(payment_processor_4_out_7), .M(payment_processor_4_m), .Clock(payment_processor_4_clock));
  payment_processor payment_processor_5 (
    .Queue_Length(Queue_Length_5), .decrement(Dequeue_Vehicle_out), .Balance(Balance_5),
    .Ticket_Price(Ticket_Price), .increment(multiplexer_5_out), .out_6(payment_processor_5_out_6),
    .out_7(payment_processor_5_out_7), .M(payment_processor_5_m), .Clock(payment_processor_5_clock));
  payment_processor payment_processor_6 (
    .Queue_Length(Queue_Length_6), .decrement(Dequeue_Vehicle_out), .Balance(Balance_6),
    .Ticket_Price(Ticket_Price), .increment(multiplexer_6_out), .out_6(payment_processor_6_out_6),
    .out_7(payment_processor_6_out_7), .M(payment_processor_6_m), .Clock(payment_processor_6_clock));
  ctr_3bit_updown ctr_3bit_updown_1 (
    .Output(Queue_Length), .M(payment_processor_1_m), .Clock(payment_processor_1_clock));
  ctr_3bit_updown ctr_3bit_updown_2 (
    .Output(Queue_Length_2), .M(payment_processor_2_m), .Clock(payment_processor_2_clock));
  ctr_3bit_updown ctr_3bit_updown_3 (
    .Output(Queue_Length_3), .M(payment_processor_3_m), .Clock(payment_processor_3_clock));
  ctr_3bit_updown ctr_3bit_updown_4 (
    .Output(Queue_Length_4), .M(payment_processor_4_m), .Clock(payment_processor_4_clock));
  ctr_3bit_updown ctr_3bit_updown_5 (
    .Output(Queue_Length_5), .M(payment_processor_5_m), .Clock(payment_processor_5_clock));
  ctr_3bit_updown ctr_3bit_updown_6 (
    .Output(Queue_Length_6), .M(payment_processor_6_m), .Clock(payment_processor_6_clock));
  LED New_Vehicle (.in(decoder_1_out1));
  LED New_Vehicle_2 (.in(decoder_1_out2));
  LED New_Vehicle_3 (.in(decoder_1_out3));
  LED New_Vehicle_4 (.in(decoder_1_out4));
  LED New_Vehicle_5 (.in(decoder_1_out5));
  LED New_Vehicle_6 (.in(decoder_1_out6));
  LED led_3 (.in(payment_processor_1_out_6));
  LED led_4 (.in(payment_processor_1_out_7));
  LED led_5 (.in(payment_processor_2_out_6));
  LED led_6 (.in(payment_processor_2_out_7));
  LED led_7 (.in(payment_processor_3_out_6));
  LED led_8 (.in(payment_processor_3_out_7));
  LED led_9 (.in(payment_processor_4_out_6));
  LED led_10 (.in(payment_processor_4_out_7));
  LED led_11 (.in(payment_processor_5_out_6));
  LED led_12 (.in(payment_processor_5_out_7));
  LED led_13 (.in(payment_processor_6_out_6));
  LED led_14 (.in(payment_processor_6_out_7));

  // Notes on the sheet:
  //   Fastag Id
  //   Team ID:
  //   INSTRUCTIONS
  //   4. Update Ticket Price
  //   Amulya Paathipati Kolar, 231CS111
  //   Preeti Mondal, 231CS144
  //   Vanshika Mittal, 231CS163
  //   Emergency Vehicle Exit
  //   1. Using Priority Vehicle button, indicate whether vehicle is of priority or not
  //   2. Input Vehicle's 16-bit Fastag ID and select Vehicle Type using button
  //   3. Enqueue Vehicle, it will be added to appropriate lane if Fastag verified
  //   5. Using Ctrl+K, simulate regular clock pulse to ensure vehicles dequeued at regular frequency
  //   TOLL PLAZA MANAGEMENT AND PAYMENT GATEWAY SYSTEM
  //   OVERALL CIRCUIT
  //   Cash Payment
  //   Fastag not verified
  //   Non-Priority Vehicle
  //   with fastag verified
  //   TRUCK LANES
  //   CAR LANES
  //   BIKE LANES
  //   Lane1
  //   Lane 2
  //   Lane3
  //   Lane4
  //   Lane5
  //   Lane6
  //   Not enough balance
  //   Payment Successful
  //   Not enough balance
  //   Payment Successful
  //   Not enough balance
  //   Payment Successful
  //   Not enough balance
  //   Payment Successful
  //   Not enough balance
  //   Payment Successful
  //   Not enough balance
  //   Payment Successful
endmodule

// Luhn's Algorithm
module luhn_gate (
  input  MSB,
  input  in_2,
  input  in_3,
  input  LSB,
  input  MSB_2,
  input  in_6,
  input  in_7,
  input  LSB_2,
  input  MSB_3,
  input  in_10,
  input  in_11,
  input  LSB_3,
  input  enable,
  input  MSB_4,
  input  in_15,
  input  in_16,
  input  LSB_4,
  output valid
);

  wire double_bcd_1_lsb_2, double_bcd_1_msb_2, double_bcd_1_out_6, double_bcd_1_out_7, double_bcd_2_lsb_2,
       double_bcd_2_msb_2, double_bcd_2_out_6, double_bcd_2_out_7, n8_bit_adder_1_s1, n8_bit_adder_1_s1_2,
       n8_bit_adder_1_s2, n8_bit_adder_1_s2_2, n8_bit_adder_1_s3, n8_bit_adder_1_s3_2, n8_bit_adder_1_s4,
       n8_bit_adder_1_s4_2, n8_bit_adder_2_s1, n8_bit_adder_2_s1_2, n8_bit_adder_2_s2, n8_bit_adder_2_s2_2,
       n8_bit_adder_2_s3, n8_bit_adder_2_s3_2, n8_bit_adder_2_s4, n8_bit_adder_2_s4_2, n8_bit_adder_3_s1_2,
       n8_bit_adder_3_s2_2, n8_bit_adder_3_s3_2, n8_bit_adder_3_s4_2, nor_1_out;

  double_bcd double_bcd_1 (
    .MSB(MSB_2), .in_2(in_6), .in_3(in_7), .LSB(LSB_2), .MSB_2(double_bcd_1_msb_2),
    .out_6(double_bcd_1_out_6), .out_7(double_bcd_1_out_7), .LSB_2(double_bcd_1_lsb_2));
  double_bcd double_bcd_2 (
    .MSB(MSB_4), .in_2(in_15), .in_3(in_16), .LSB(LSB_4), .MSB_2(double_bcd_2_msb_2),
    .out_6(double_bcd_2_out_6), .out_7(double_bcd_2_out_7), .LSB_2(double_bcd_2_lsb_2));
  _8_bit_adder u_8_bit_adder_1 (
    .A4(1'b0), .A3(1'b0), .A2(1'b0), .A1(1'b0), .A4_2(MSB), .A3_2(in_2), .A2_2(in_3), .A1_2(LSB),
    .B4(double_bcd_1_msb_2), .B3(double_bcd_1_out_6), .B2(double_bcd_1_out_7), .B1(double_bcd_1_lsb_2),
    .S4(n8_bit_adder_1_s4), .S3(n8_bit_adder_1_s3), .S2(n8_bit_adder_1_s2), .S1(n8_bit_adder_1_s1),
    .S4_2(n8_bit_adder_1_s4_2), .S3_2(n8_bit_adder_1_s3_2), .S2_2(n8_bit_adder_1_s2_2),
    .S1_2(n8_bit_adder_1_s1_2));
  _8_bit_adder u_8_bit_adder_2 (
    .A4(n8_bit_adder_1_s4), .A3(n8_bit_adder_1_s3), .A2(n8_bit_adder_1_s2), .A1(n8_bit_adder_1_s1),
    .A4_2(n8_bit_adder_1_s4_2), .A3_2(n8_bit_adder_1_s3_2), .A2_2(n8_bit_adder_1_s2_2),
    .A1_2(n8_bit_adder_1_s1_2), .B4(MSB_3), .B3(in_10), .B2(in_11), .B1(LSB_3), .S4(n8_bit_adder_2_s4),
    .S3(n8_bit_adder_2_s3), .S2(n8_bit_adder_2_s2), .S1(n8_bit_adder_2_s1), .S4_2(n8_bit_adder_2_s4_2),
    .S3_2(n8_bit_adder_2_s3_2), .S2_2(n8_bit_adder_2_s2_2), .S1_2(n8_bit_adder_2_s1_2));
  _8_bit_adder u_8_bit_adder_3 (
    .A4(n8_bit_adder_2_s4), .A3(n8_bit_adder_2_s3), .A2(n8_bit_adder_2_s2), .A1(n8_bit_adder_2_s1),
    .A4_2(n8_bit_adder_2_s4_2), .A3_2(n8_bit_adder_2_s3_2), .A2_2(n8_bit_adder_2_s2_2),
    .A1_2(n8_bit_adder_2_s1_2), .B4(double_bcd_2_msb_2), .B3(double_bcd_2_out_6), .B2(double_bcd_2_out_7),
    .B1(double_bcd_2_lsb_2), .S4_2(n8_bit_adder_3_s4_2), .S3_2(n8_bit_adder_3_s3_2),
    .S2_2(n8_bit_adder_3_s2_2), .S1_2(n8_bit_adder_3_s1_2));  // open: S4, S3, S2, S1
  nor nor_1 (nor_1_out, n8_bit_adder_3_s4_2, n8_bit_adder_3_s3_2, n8_bit_adder_3_s2_2, n8_bit_adder_3_s1_2);
  and and_1 (valid, enable, nor_1_out);

  // Notes on the sheet:
  //   Verification of account number using Luhn's algorithm
endmodule

// x2
module double_bcd (
  input  MSB,
  input  in_2,
  input  in_3,
  input  LSB,
  output MSB_2,
  output out_6,
  output out_7,
  output LSB_2
);

  wire and_1_out, and_2_out, and_3_out, and_4_out, and_5_out, and_6_out, and_7_out, not_1_out, not_2_out,
       not_3_out, not_4_out, or_2_out, or_3_out;

  not not_1 (not_1_out, MSB);
  not not_2 (not_2_out, in_2);
  not not_3 (not_3_out, in_3);
  not not_4 (not_4_out, LSB);
  and and_1 (and_1_out, MSB, LSB);
  and and_2 (and_2_out, in_2, not_3_out, not_4_out);
  or or_1 (MSB_2, and_1_out, and_2_out);
  and and_3 (and_3_out, MSB, not_4_out);
  or or_2 (or_2_out, not_2_out, LSB);
  and and_4 (and_4_out, or_2_out, in_3);
  and and_5 (and_5_out, not_1_out, not_2_out, LSB);
  and and_6 (and_6_out, in_2, in_3, not_4_out);
  and and_7 (and_7_out, in_2, or_3_out);
  or or_3 (or_3_out, in_3, LSB);
  or or_4 (out_6, and_3_out, and_4_out);
  or or_5 (out_7, and_5_out, and_3_out, and_6_out);
  or or_6 (LSB_2, MSB, and_7_out);

  // Notes on the sheet:
  //   Circuit Used to Double BCD numbers and add sum of digits if double digit double
endmodule

// FA
module full_adder (
  input  A,
  input  B,
  input  Cin,
  output S,
  output C
);

  wire and_1_out, and_2_out, xor_1_out;

  xor xor_1 (xor_1_out, A, B);
  and and_1 (and_1_out, A, B);
  xor xor_2 (S, xor_1_out, Cin);
  and and_2 (and_2_out, xor_1_out, Cin);
  or or_1 (C, and_2_out, and_1_out);

  // Notes on the sheet:
  //   Full Adder
endmodule

// 4 bit adder
module _4_bit_adder (
  input  A4,
  input  A3,
  input  A2,
  input  A1,
  input  B4,
  input  B3,
  input  B2,
  input  B1,
  input  Cin,
  output C,
  output S4,
  output S3,
  output S2,
  output S1
);

  wire full_adder_2_c, full_adder_3_c, full_adder_4_c;

  full_adder full_adder_1 (.A(A4), .B(B4), .Cin(full_adder_2_c), .S(S4), .C(C));
  full_adder full_adder_2 (.A(A3), .B(B3), .Cin(full_adder_3_c), .S(S3), .C(full_adder_2_c));
  full_adder full_adder_3 (.A(A2), .B(B2), .Cin(full_adder_4_c), .S(S2), .C(full_adder_3_c));
  full_adder full_adder_4 (.A(A1), .B(B1), .Cin(Cin), .S(S1), .C(full_adder_4_c));

  // Notes on the sheet:
  //   4-Bit Adder
endmodule

// 8 bit adder
module _8_bit_adder (
  input  A4,
  input  A3,
  input  A2,
  input  A1,
  input  A4_2,
  input  A3_2,
  input  A2_2,
  input  A1_2,
  input  B4,
  input  B3,
  input  B2,
  input  B1,
  output S4,
  output S3,
  output S2,
  output S1,
  output S4_2,
  output S3_2,
  output S2_2,
  output S1_2
);

  wire and_1_out, and_2_out, n4_bit_adder_1_c, n4_bit_adder_1_s1, n4_bit_adder_1_s2, n4_bit_adder_1_s3,
       n4_bit_adder_1_s4, n4_bit_adder_3_c, or_1_out, xor_1_out;

  _4_bit_adder u_4_bit_adder_1 (
    .A4(A4_2), .A3(A3_2), .A2(A2_2), .A1(A1_2), .B4(B4), .B3(B3), .B2(B2), .B1(B1), .Cin(1'b0),
    .C(n4_bit_adder_1_c), .S4(n4_bit_adder_1_s4), .S3(n4_bit_adder_1_s3), .S2(n4_bit_adder_1_s2),
    .S1(n4_bit_adder_1_s1));
  _4_bit_adder u_4_bit_adder_2 (
    .A4(A4), .A3(A3), .A2(A2), .A1(A1), .B4(1'b0), .B3(1'b0), .B2(1'b0), .B1(xor_1_out), .Cin(1'b0), .S4(S4),
    .S3(S3), .S2(S2), .S1(S1));  // open: C
  and and_1 (and_1_out, n4_bit_adder_1_s4, n4_bit_adder_1_s3);
  and and_2 (and_2_out, n4_bit_adder_1_s4, n4_bit_adder_1_s2);
  or or_1 (or_1_out, n4_bit_adder_1_c, and_1_out, and_2_out);
  _4_bit_adder u_4_bit_adder_3 (
    .A4(1'b0), .A3(or_1_out), .A2(or_1_out), .A1(1'b0), .B4(n4_bit_adder_1_s4), .B3(n4_bit_adder_1_s3),
    .B2(n4_bit_adder_1_s2), .B1(n4_bit_adder_1_s1), .Cin(1'b0), .C(n4_bit_adder_3_c), .S4(S4_2), .S3(S3_2),
    .S2(S2_2), .S1(S1_2));
  xor xor_1 (xor_1_out, n4_bit_adder_1_c, n4_bit_adder_3_c);

  // Notes on the sheet:
  //   Circuit to add an 8-bit BCD number to 4-bit BCD number
endmodule

// Comparator
module compartor_4_bit (
  input  A3,
  input  B3,
  input  A2,
  input  B2,
  input  A1,
  input  B1,
  input  A0,
  input  B0,
  output A_B,
  output A_B_2,
  output A_B_3
);

  wire and_1_out, and_2_out, and_3_out, and_4_out, and_5_out, and_6_out, and_7_out, and_8_out, and_10_out,
       and_11_out, and_12_out, and_13_out, and_14_out, and_15_out, nor_1_out, nor_2_out, nor_3_out,
       nor_4_out, not_1_out, not_2_out, not_3_out, not_4_out, not_5_out, not_6_out, not_7_out, not_8_out;

  not not_1 (not_1_out, A3);
  not not_2 (not_2_out, B3);
  not not_3 (not_3_out, A2);
  not not_4 (not_4_out, B2);
  not not_5 (not_5_out, A1);
  not not_6 (not_6_out, B1);
  not not_7 (not_7_out, A0);
  not not_8 (not_8_out, B0);
  and and_1 (and_1_out, not_1_out, B3);
  and and_2 (and_2_out, A3, not_2_out);
  and and_3 (and_3_out, not_3_out, B2);
  and and_4 (and_4_out, A2, not_4_out);
  and and_5 (and_5_out, not_5_out, B1);
  and and_6 (and_6_out, A1, not_6_out);
  and and_7 (and_7_out, not_7_out, B0);
  and and_8 (and_8_out, A0, not_8_out);
  nor nor_1 (nor_1_out, and_1_out, and_2_out);
  nor nor_2 (nor_2_out, and_3_out, and_4_out);
  nor nor_3 (nor_3_out, and_5_out, and_6_out);
  nor nor_4 (nor_4_out, and_7_out, and_8_out);
  and and_9 (A_B_3, nor_1_out, nor_2_out, nor_3_out, nor_4_out);
  and and_10 (and_10_out, nor_1_out, and_3_out);
  and and_11 (and_11_out, nor_1_out, and_4_out);
  and and_12 (and_12_out, nor_1_out, nor_2_out, and_5_out);
  and and_13 (and_13_out, nor_1_out, nor_2_out, and_6_out);
  and and_14 (and_14_out, nor_1_out, nor_2_out, nor_3_out, and_7_out);
  and and_15 (and_15_out, nor_1_out, nor_2_out, nor_3_out, and_8_out);
  or or_1 (A_B, and_1_out, and_10_out, and_12_out, and_14_out);
  or or_2 (A_B_2, and_2_out, and_11_out, and_13_out, and_15_out);

  // Notes on the sheet:
  //   4-Bit Comparator
endmodule

module balance_checker (
  input  [3:0] Balance,
  input  [3:0] Ticket,
  output out_3,
  output out_4
);

  wire compartor_4_bit_1_a_b_2, compartor_4_bit_1_a_b_3;

  compartor_4_bit compartor_4_bit_1 (
    .A3(Balance[3]), .B3(Ticket[3]), .A2(Balance[2]), .B2(Ticket[2]), .A1(Balance[1]), .B1(Ticket[1]),
    .A0(Balance[0]), .B0(Ticket[0]), .A_B(out_3), .A_B_2(compartor_4_bit_1_a_b_2),
    .A_B_3(compartor_4_bit_1_a_b_3));
  or or_1 (out_4, compartor_4_bit_1_a_b_2, compartor_4_bit_1_a_b_3);

  // Other names for the same wires on the sheet: b0 = Balance[0]; b1 = Balance[1]; b2 = Balance[2]; b3 = Balance[3];
  //   t0 = Ticket[0]; t1 = Ticket[1]; t2 = Ticket[2]; t3 = Ticket[3]

  // Notes on the sheet:
  //   Checking Available Balance
  //   Balance Insufficient
  //   Payment Succesful
endmodule

module segregate (
  input  in_1,
  output trucks,
  output cars,
  output bikes
);

  wire d_ff_1_q, d_ff_1_qn, d_ff_2_q, d_ff_2_qn, not_1_out, not_2_out;

  not not_1 (not_1_out, d_ff_1_q);
  D_Flip_Flop d_ff_1 (.clk(in_1), .D(d_ff_1_qn), .Q(d_ff_1_q), .Qn(d_ff_1_qn));  // open: preset, en, reset
  not not_2 (not_2_out, d_ff_2_q);
  D_Flip_Flop d_ff_2 (.clk(d_ff_1_qn), .D(d_ff_2_qn), .Q(d_ff_2_q), .Qn(d_ff_2_qn));  // open: preset, en, reset
  and and_1 (trucks, d_ff_1_q, not_2_out);
  and and_2 (cars, not_1_out, d_ff_2_q);
  and and_3 (bikes, d_ff_1_q, d_ff_2_q);

  // Notes on the sheet:
  //   Segregate Vehicles
endmodule

module vehicle_priority (
  input  in_1,
  output Priority_Vehicle,
  output Common_Vehicle
);

  wire d_ff_1_q, d_ff_1_qn, d_ff_2_q, d_ff_2_qn, not_1_out, not_2_out;

  not not_1 (not_1_out, d_ff_1_q);
  D_Flip_Flop d_ff_1 (.clk(in_1), .D(d_ff_1_qn), .Q(d_ff_1_q), .Qn(d_ff_1_qn));  // open: preset, en, reset
  not not_2 (not_2_out, d_ff_2_q);
  D_Flip_Flop d_ff_2 (.clk(d_ff_1_qn), .D(d_ff_2_qn), .Q(d_ff_2_q), .Qn(d_ff_2_qn));  // open: preset, en, reset
  and and_1 (Priority_Vehicle, d_ff_1_q, not_2_out);
  and and_2 (Common_Vehicle, not_1_out, d_ff_2_q);

  // Notes on the sheet:
  //   Circuit to check if vehicle is a priority vehicle
endmodule

// comparator
module compartor_3_bit (
  input  [2:0] Lane_2,
  input  [2:0] Lane_1,
  output [2:0] Output
);

  wire and_1_out, and_2_out, and_3_out, and_4_out, and_5_out, and_6_out, and_7_out, and_8_out, and_9_out,
       and_10_out, and_11_out, nor_1_out, nor_2_out, nor_3_out, not_1_out, not_2_out, not_3_out, not_4_out,
       not_5_out, not_6_out, or_2_out;

  not not_1 (not_1_out, Lane_1[2]);
  not not_2 (not_2_out, Lane_2[2]);
  not not_3 (not_3_out, Lane_1[1]);
  not not_4 (not_4_out, Lane_2[1]);
  not not_5 (not_5_out, Lane_1[0]);
  not not_6 (not_6_out, Lane_2[0]);
  and and_1 (and_1_out, not_1_out, Lane_2[2]);
  and and_2 (and_2_out, Lane_1[2], not_2_out);
  and and_3 (and_3_out, not_3_out, Lane_2[1]);
  and and_4 (and_4_out, Lane_1[1], not_4_out);
  and and_5 (and_5_out, not_5_out, Lane_2[0]);
  and and_6 (and_6_out, Lane_1[0], not_6_out);
  nor nor_1 (nor_1_out, and_1_out, and_2_out);
  nor nor_2 (nor_2_out, and_3_out, and_4_out);
  nor nor_3 (nor_3_out, and_5_out, and_6_out);
  and and_7 (and_7_out, nor_1_out, and_3_out);
  and and_8 (and_8_out, nor_1_out, and_4_out);
  and and_9 (and_9_out, nor_1_out, nor_2_out, and_5_out);
  and and_10 (and_10_out, nor_1_out, nor_2_out, and_6_out);
  and and_11 (and_11_out, nor_1_out, nor_2_out, nor_3_out);
  or or_1 (Output[0], and_1_out, and_7_out, and_9_out);
  or or_2 (or_2_out, and_2_out, and_8_out, and_10_out);
  or or_3 (Output[1], or_2_out, and_11_out);

  assign Output[2] = 1'b0;

  // Other names for the same wires on the sheet: A0 = Lane_1[0]; A1 = Lane_1[1]; A2 = Lane_1[2]; B0 = Lane_2[0];
  //   B1 = Lane_2[1]; B2 = Lane_2[2]; A___B = Output[0]; A____B = Output[1]

  // Notes on the sheet:
  //   3 bit Comparator
endmodule

// counter
module ctr_3bit_updown (
  input  M,
  input  Clock,
  output [2:0] Output
);

  wire and_1_out, and_2_out, and_3_out, and_4_out, not_1_out, or_1_out, or_2_out, t_ff_1_qn, t_ff_2_qn;

  not not_1 (not_1_out, M);
  T_Flip_Flop t_ff_1 (.clk(Clock), .T(1'b1), .Q(Output[0]), .Qn(t_ff_1_qn));  // open: preset, reset, en
  and and_1 (and_1_out, M, t_ff_1_qn);
  and and_2 (and_2_out, not_1_out, Output[0]);
  or or_1 (or_1_out, and_2_out, and_1_out);
  T_Flip_Flop t_ff_2 (.clk(Clock), .T(or_1_out), .Q(Output[1]), .Qn(t_ff_2_qn));  // open: preset, reset, en
  and and_3 (and_3_out, and_2_out, Output[1]);
  and and_4 (and_4_out, t_ff_2_qn, and_1_out);
  or or_2 (or_2_out, and_3_out, and_4_out);
  T_Flip_Flop t_ff_3 (.clk(Clock), .T(or_2_out), .Q(Output[2]));  // open: Qn, preset, reset, en

  // Other names for the same wires on the sheet: B0 = Output[0]; B1 = Output[1]; B2 = Output[2]

  // Notes on the sheet:
  //   3 bit up-down counter used to maintain queue length
endmodule

// Payment Processor
module payment_processor (
  input  decrement,
  input  [2:0] Queue_Length,
  input  [3:0] Ticket_Price,
  input  increment,
  output [3:0] Balance,
  output out_6,
  output out_7,
  output M,
  output Clock
);

  wire and_1_out, and_2_out, and_4_out, d_ff_1_q, multiplexer_1_out, not_1_out, not_2_out, not_3_out,
       or_1_out;

  or or_1 (or_1_out, Queue_Length[2], Queue_Length[1], Queue_Length[0]);
  not not_1 (not_1_out, decrement);
  Random #(.width(4), .trigger("falling")) random_1 (.clk(decrement), .next(or_1_out), .out(Balance));  // open: clr
  and and_1 (and_1_out, or_1_out, out_7, decrement);
  not not_2 (not_2_out, decrement);
  D_Flip_Flop d_ff_1 (
    .clk(decrement), .D(decrement), .Q(d_ff_1_q), .preset(and_1_out), .reset(not_1_out));  // open: Qn, en
  balance_checker Balance_Checker (.Balance(Balance), .Ticket(Ticket_Price), .out_3(out_6), .out_4(out_7));
  and and_2 (and_2_out, 1'b1, 1'b1, 1'b1, Queue_Length[2], Queue_Length[1], Queue_Length[0]);
  Multiplexer multiplexer_1 (.in0(1'b0), .in1(increment), .out(multiplexer_1_out), .sel(increment), .en(not_3_out));
  not not_3 (not_3_out, and_2_out);
  and and_3 (M, out_7, multiplexer_1_out, not_2_out);
  xor xor_1 (Clock, d_ff_1_q, and_4_out);
  and and_4 (and_4_out, not_3_out, multiplexer_1_out);

  // Other names for the same wires on the sheet: B0 = Queue_Length[0]; B1 = Queue_Length[1]; B2 = Queue_Length[2]

  // Notes on the sheet:
  //   Payment Processor
  //   Module updates input going into up/down counter based on existing conditions
  //   Not enough balance
  //   Payment Successful
endmodule

// Lane Segregator
module lane_separation (
  input  [2:0] Lane_1,
  input  [2:0] Lane_3,
  input  [2:0] Lane_5,
  input  [1:0] Vehicle_type,
  input  [2:0] Lane_2,
  input  [2:0] Lane_4,
  input  [2:0] Lane_6,
  output [2:0] Final_Lane__Binary
);

  wire [2:0] compartor_3_bit_1_output, multiplexer_1_out, multiplexer_2_out;

  Multiplexer #(.select(2), .width(3)) multiplexer_1 (
    .in0(Lane_1), .in1(Lane_3), .in2(Lane_5), .in3(3'b000), .out(multiplexer_1_out), .sel(Vehicle_type));  // open: en
  Multiplexer #(.select(2), .width(3)) multiplexer_2 (
    .in0(Lane_2), .in1(Lane_4), .in2(Lane_6), .in3(3'b000), .out(multiplexer_2_out), .sel(Vehicle_type));  // open: en
  compartor_3_bit compartor_3_bit_1 (
    .Lane_1(multiplexer_1_out), .Lane_2(multiplexer_2_out), .Output(compartor_3_bit_1_output));
  Adder #(.width(3)) adder_1 (
    .a({Vehicle_type, 1'b0}), .b(compartor_3_bit_1_output), .out(Final_Lane__Binary));  // open: cin, cout

  // Notes on the sheet:
  //   Module to pick final lane to direct incoming traffic into
endmodule
